# Fritzing sketch LaserLockAuth (saved by Fritzing 0.9.3b)

parts:
  Mod1 = laser receiver [package=THT]
  Mod2 = KY-008 Laser Transmitter Module [package="Breakout board"]
  R2 = Resistor [tolerance=±5% resistance=220 package="0805 [SMD]"]
  Part2 = Arduino Uno (Rev3)
  LED1 = LED - 3mm [color="Red (633nm)" package="3 mm [THT]"]
  LED2 = LED - 3mm [color="Green (555nm)" package="3 mm [THT]"]
  R1 = Resistor [tolerance=±5% resistance=220 package="0805 [SMD]"]
  S1 = Pushbutton [package=THT]

nets:
  N1: Mod1.pin1, Mod2.-, Part2.GND, LED1.cathode, LED2.cathode, S1.leg1
  N2: Mod1.pin2, Part2.D9_PWM
  N3: Mod1.pin3, Mod2.S, Part2.5V
  N4: Mod2.NC, Part2.D12/MISO
  N5: R2.Pin_0, LED2.anode
  N6: R2.Pin_1, Part2.D11_PWM/MOSI
  N7: Part2.D8, S1.leg0
  N8: Part2.D10_PWM/SS, R1.Pin_1
  N9: LED1.anode, R1.Pin_0

custom parts:
  laser receiver: Generic non modulated laser receiver module.
  KY-008 Laser Transmitter Module: KY-008 Laser Transmitter Module, emits a dot shaped red laser beam.
